// Logisim project watermelon_one.circ as structural Verilog: 4 circuits, main circuit main
module main (
);

  octal_D_flip_flop octal_d_flip_flop_1 ();  // open: OE, C, D, O
endmodule

module octal_D_flip_flop (
  input  OE,
  input  C,
  input  [7:0] D,
  output [7:0] O
);

  wire [7:0] d_ff_1_q;

  D_Flip_Flop d_ff_1 (.D(D[0]), .clk(C), .Q(d_ff_1_q[0]));  // open: Qn, preset, reset
  D_Flip_Flop d_ff_2 (.D(D[1]), .clk(C), .Q(d_ff_1_q[1]));  // open: Qn, preset, reset
  D_Flip_Flop d_ff_3 (.D(D[2]), .clk(C), .Q(d_ff_1_q[2]));  // open: Qn, preset, reset
  D_Flip_Flop d_ff_4 (.D(D[3]), .clk(C), .Q(d_ff_1_q[3]));  // open: Qn, preset, reset
  D_Flip_Flop d_ff_5 (.D(D[4]), .clk(C), .Q(d_ff_1_q[4]));  // open: Qn, preset, reset
  D_Flip_Flop d_ff_6 (.D(D[5]), .clk(C), .Q(d_ff_1_q[5]));  // open: Qn, preset, reset
  D_Flip_Flop d_ff_7 (.D(D[6]), .clk(C), .Q(d_ff_1_q[6]));  // open: Qn, preset, reset
  D_Flip_Flop d_ff_8 (.D(D[7]), .clk(C), .Q(d_ff_1_q[7]));  // open: Qn, preset, reset
  assign O = OE ? d_ff_1_q : 8'bz;  // Controlled_Buffer controlled_buffer_1
endmodule

module register_8_bit (
  input  OE,
  input  WE,
  input  C,
  input  [7:0] D,
  output [7:0] O
);

  wire and_1_out;

  and and_1 (and_1_out, WE, C);
  octal_D_flip_flop octal_d_flip_flop_1 (.OE(OE), .C(and_1_out), .D(D), .O(O));
endmodule

module sram (
);

  RAM ram_1 ();  // open: addr, we, oe, clk, din, dout
endmodule
